// Logisim project regfile.circ as structural Verilog: 1 circuit, main circuit regfile
module regfile (
  input  [4:0] ReadIndex1,
  input  [4:0] ReadIndex2,
  input  [4:0] WriteIndex,
  input  [31:0] WriteData,
  input  RegWEn,
  input  clk,
  output [31:0] ra,
  output [31:0] sp,
  output [31:0] t0,
  output [31:0] t1,
  output [31:0] t2,
  output [31:0] s0,
  output [31:0] s1,
  output [31:0] a0,
  output [31:0] ReadData1,
  output [31:0] ReadData2
);

  wire decoder_1_out1, decoder_1_out2, decoder_1_out3, decoder_1_out4, decoder_1_out5, decoder_1_out6,
       decoder_1_out7, decoder_1_out8, decoder_1_out9, decoder_1_out10, decoder_1_out11, decoder_1_out12,
       decoder_1_out13, decoder_1_out14, decoder_1_out15, decoder_1_out16, decoder_1_out17, decoder_1_out18,
       decoder_1_out19, decoder_1_out20, decoder_1_out21, decoder_1_out22, decoder_1_out24, decoder_1_out25,
       decoder_1_out26, decoder_1_out27, decoder_1_out28, decoder_1_out29, decoder_1_out30, decoder_1_out31,
       undriven;

  Decoder #(.select(5)) decoder_1 (
    .out1(decoder_1_out1), .out2(decoder_1_out2), .out3(decoder_1_out3), .out4(decoder_1_out4),
    .out5(decoder_1_out5), .out6(decoder_1_out6), .out7(decoder_1_out7), .out8(decoder_1_out8),
    .out9(decoder_1_out9), .out10(decoder_1_out10), .out11(decoder_1_out11), .out12(decoder_1_out12),
    .out13(decoder_1_out13), .out14(decoder_1_out14), .out15(decoder_1_out15), .out16(decoder_1_out16),
    .out17(decoder_1_out17), .out18(decoder_1_out18), .out19(decoder_1_out19), .out20(decoder_1_out20),
    .out21(decoder_1_out21), .out22(decoder_1_out22), .out23(decoder_1_out22), .out24(decoder_1_out24),
    .out25(decoder_1_out25), .out26(decoder_1_out26), .out27(decoder_1_out27), .out28(decoder_1_out28),
    .out29(decoder_1_out29), .out30(decoder_1_out30), .out31(decoder_1_out31), .sel(WriteIndex), .en(RegWEn));  // open: out0
  Register #(.width(32)) register_1 (.D(WriteData), .en(decoder_1_out1), .clk(clk));  // open: Q, clr
  Multiplexer multiplexer_1 ();  // open: in0, in1, out, sel
  Register #(.width(32)) register_2 (.D(WriteData), .en(decoder_1_out2), .clk(clk));  // open: Q, clr
  Register #(.width(32)) register_3 (.D(WriteData), .en(decoder_1_out3), .clk(clk));  // open: Q, clr
  Register #(.width(32)) register_4 (.D(WriteData), .en(decoder_1_out31), .clk(clk));  // open: Q, clr
  Register #(.width(32)) register_5 (.D(WriteData), .en(decoder_1_out4), .clk(clk));  // open: Q, clr
  Register #(.width(32)) register_6 (.D(WriteData), .en(decoder_1_out30), .clk(clk));  // open: Q, clr
  Register #(.width(32)) register_7 (.D(WriteData), .en(decoder_1_out5), .clk(clk));  // open: Q, clr
  Register #(.width(32)) register_8 (.D(WriteData), .en(decoder_1_out29), .clk(clk));  // open: Q, clr
  Register #(.width(32)) register_9 (.D(WriteData), .en(decoder_1_out6), .clk(clk));  // open: Q, clr
  Register #(.width(32)) register_10 (.D(WriteData), .en(decoder_1_out28), .clk(clk));  // open: Q, clr
  Register #(.width(32)) register_11 (.D(WriteData), .en(decoder_1_out7), .clk(clk));  // open: Q, clr
  Register #(.width(32)) register_12 (.D(WriteData), .en(decoder_1_out27), .clk(clk));  // open: Q, clr
  Register #(.width(32)) register_13 (.D(WriteData), .en(decoder_1_out8), .clk(undriven));  // open: Q, clr
  Register #(.width(32)) register_14 (.D(WriteData), .en(decoder_1_out26), .clk(clk));  // open: Q, clr
  Register #(.width(32)) register_15 (.D(WriteData), .en(decoder_1_out9), .clk(clk));  // open: Q, clr
  Register #(.width(32)) register_16 (.D(WriteData), .en(decoder_1_out25), .clk(clk));  // open: Q, clr
  Register #(.width(32)) register_17 (.D(WriteData), .en(decoder_1_out10), .clk(clk));  // open: Q, clr
  Register #(.width(32)) register_18 (.D(WriteData), .en(decoder_1_out24), .clk(clk));  // open: Q, clr
  Register #(.width(32)) register_19 (.D(WriteData), .clk(clk));  // open: en, Q, clr
  Register #(.width(32)) register_20 (.D(WriteData), .en(decoder_1_out22), .clk(clk));  // open: Q, clr
  Register #(.width(32)) register_21 (.D(WriteData), .en(decoder_1_out11), .clk(clk));  // open: Q, clr
  Register #(.width(32)) register_22 (.D(WriteData), .en(decoder_1_out12), .clk(clk));  // open: Q, clr
  Register #(.width(32)) register_23 (.D(WriteData), .en(decoder_1_out13), .clk(clk));  // open: Q, clr
  Register #(.width(32)) register_24 (.D(WriteData), .en(decoder_1_out14), .clk(clk));  // open: Q, clr
  Register #(.width(32)) register_25 (.D(WriteData), .en(decoder_1_out15), .clk(clk));  // open: Q, clr
  Register #(.width(32)) register_26 (.D(WriteData), .en(decoder_1_out16), .clk(clk));  // open: Q, clr
  Register #(.width(32)) register_27 (.D(WriteData), .en(decoder_1_out17), .clk(clk));  // open: Q, clr
  Register #(.width(32)) register_28 (.D(WriteData), .en(decoder_1_out18), .clk(clk));  // open: Q, clr
  Register #(.width(32)) register_29 (.D(WriteData), .en(decoder_1_out19), .clk(clk));  // open: Q, clr
  Register #(.width(32)) register_30 (.D(WriteData), .en(decoder_1_out20), .clk(clk));  // open: Q, clr
  Register #(.width(32)) register_31 (.D(WriteData), .en(decoder_1_out21), .clk(clk));  // open: Q, clr
  Register #(.width(32)) register_32 (.D(WriteData), .en(decoder_1_out22), .clk(clk));  // open: Q, clr

  assign ReadData1 = {32{1'b0}};

  // Notes on the sheet:
  //   INPUTS to your circuit
  //   DON'T CHANGE THE LOCATIONS OF THE INPUTS AND OUTPUTS!
  //   These are DEBUG/TEST outputs from your circuit.
  //   OUTPUTS from your circuit
endmodule
